# Fritzing sketch delay_switch (saved by Fritzing 0.9.3b)
breadboards: 1

parts:
  S1 = Pushbutton [package=THT]
  R1 = Resistor [tolerance=±5% resistance=220 package=THT]
  Part1 = Arduino Uno (Rev3)

nets:
  N1: S1.leg0, R1.Pin_1, Part1.D8
  N2: S1.leg1, Part1.5V
  N3: R1.Pin_0, Part1.GND
